# Fritzing sketch candelabra (saved by Fritzing 1.0.6)
circuit board: 2cm x 11cm
breadboards: 2

parts:
  5K = Rotary Potentiometer (Small) [maximum_resistance=5kΩ knob_status=50% power=0.5W package=THT]
  104 = Ceramic Capacitor [capacitance=100nF voltage=16V package="200 mil [THT, multilayer]"]
  x = PJ-301M [part_number=PJ-301M]
  CV = PJ-301M [part_number=PJ-301M]
  Z = PJ-301M [part_number=PJ-301M]
  Y = PJ-301M [part_number=PJ-301M]
  Shrouded_Male = shrouded pin header, 10 pins [form="♂ (shrouded male)"]
  5187 = Diode [package=diode-1n4148]
  1K = Resistor [tolerance=±5% power=0.25W resistance=1k package=THT]
  LED1 = LED - 5mm [color="Red (660nm)" current=0.030A package="5 mm [THT]"]
  LED2 = LED - 5mm [color="Red (660nm)" current=0.030A package="5 mm [THT]"]
  5187_2 = Diode [package=diode-1n4148]
  100uF1 = Electrolytic Capacitor [capacitance=0.1mF voltage=35V package="100 mil [THT, electrolytic]"]
  S6 = SPST Switch [package=switch-spdt_kit]
  1000uF = Electrolytic Capacitor [capacitance=1mF voltage=35V package="100 mil [THT, electrolytic]"]
  1000uF2 = Electrolytic Capacitor [capacitance=1mF voltage=35V package="100 mil [THT, electrolytic]"]
  470uf = Electrolytic Capacitor [capacitance=0.47mF voltage=35V package="100 mil [THT, electrolytic]"]
  Vactrol2 = VTL5C1
  2N3904 = NPN-Transistor [package="TO92 [THT]"]
  2N3904_2 = NPN-Transistor [package="TO92 [THT]"]
  2N3904_3 = NPN-Transistor [package="TO92 [THT]"]
  BAT46 = Diode [package=diode-1n4148]
  BAT46_2 = Diode [package=diode-1n4148]
  BAT46_3 = Diode [package=diode-1n4148]
  LED3 = LED - 5mm [color="Red (660nm)" current=0.030A package="5 mm [THT]"]
  1k = Resistor [tolerance=±5% power=0.25W resistance=1k package=THT]
  100 = Resistor [tolerance=±1% power=0.25W resistance=100 package=THT]
  1000uF_2 = Electrolytic Capacitor [capacitance=1mF voltage=16V package="100 mil [THT, electrolytic]"]

nets:
  N1: 5K.leg1, 104.0, 1K.Pin_0, 100uF1.+, Vactrol2.Pin_4, 1k.Pin_0, 100.Pin_0
  N2: 5K.wiper, 1000uF2.+, 470uf.+, Vactrol2.Pin_3, 2N3904.E, BAT46_3.A, LED3.anode
  GND: 104.1, x.Pin_1, CV.Pin_1, Z.Pin_1, Y.Pin_1, Shrouded_Male.pin2, Shrouded_Male.pin3, Shrouded_Male.pin4, Shrouded_Male.pin7, Shrouded_Male.pin8, Shrouded_Male.pin9, 100uF1.-, S6.P, 1000uF.-, Vactrol2.Pin_1, 2N3904.C, 2N3904_2.C, 2N3904_3.C, 1000uF_2.-
  N3: x.Pin_3, BAT46.C
  N4: CV.Pin_3, 5187_2.A
  N5: Z.Pin_3, BAT46_3.C
  N6: Y.Pin_3, BAT46_2.C
  N7: Shrouded_Male.pin1, Shrouded_Male.pin10
  12V: Shrouded_Male.pin5, Shrouded_Male.pin6, 5187.A
  N8: 5187.C, 100.Pin_1
  N9: 1K.Pin_1, LED1.anode, 2N3904_3.E, BAT46.A, 1000uF_2.+
  N10: LED1.cathode, 2N3904_2.B
  N11: LED2.cathode, 2N3904.B
  N12: LED2.anode, 1000uF.+, 2N3904_2.E, BAT46_2.A, 1k.Pin_1
  N13: 5187_2.C, Vactrol2.Pin_2
  N14: S6.O, 470uf.-
  N15: S6.S, 1000uF2.-
  N16: 2N3904_3.B, LED3.cathode

notes:
  jlcjlcjlcjlcjlc

custom parts:
  PJ-301M: Phone power jack.
  VTL5C1: Xvive5C1-R OPTO-ISOLATOR SPECICATION.
